# Fritzing sketch Esquemático fritzing (saved by Fritzing 1.0.5)

parts:
  A1 = ESP32-S3-1-N16R8-CAM
  LCD1 = 2.8" SPI TFT Module [part_number=MSP2807]
  S13 = Load Sensor - 50kg [part_number=SEN-10245]
  Componente4 = HX711 Weighing Sensor Module
  S14 = Load Sensor - 50kg [part_number=SEN-10245]
  S15 = Load Sensor - 50kg [part_number=SEN-10245]
  S16 = Load Sensor - 50kg [part_number=SEN-10245]

nets:
  N1: A1.Pin_1, LCD1.pin1, LCD1.pin8, Componente4.VCC
  N2: A1.Pin_10, Componente4.DO/RX
  N3: A1.Pin_11, Componente4.CK/TX
  N4: A1.Pin_19, LCD1.pin13
  N5: A1.Pin_21, A1.Pin_22, LCD1.pin2, LCD1.pin14, Componente4.GND
  N6: A1.Pin_23, LCD1.pin11
  N7: A1.Pin_24, LCD1.pin3
  N8: A1.Pin_25, LCD1.pin4
  N9: A1.Pin_34, LCD1.pin12
  N10: A1.Pin_35, LCD1.pin6
  N11: A1.Pin_36, LCD1.pin7
  N12: A1.Pin_37, LCD1.pin10
  N13: A1.Pin_38, LCD1.pin5
  N14: S13.B, Componente4.A-, S14.R, S15.B, S15.W, S15.R, S16.W
  N15: S13.W, S13.R, Componente4.A+, S14.B, S14.W, S16.B, S16.R

notes:
  Balança de Peso
  Microcontrolador
  Tela LCD 2.8" Touchscreen

custom parts:
  ESP32-S3-1-N16R8-CAM: ESP32-S3 CAM development board WiFi Bluetooth module onboard ESP32-S3-1 N16R8 module dual TYPE-C interface.
  2.8" SPI TFT Module: A generic 2.8 inch LCD TFT 320x240 display with touchscreen and SD card slot. Uses the ILI9341 controller, like the Adafruit displays of this size uses.
  Load Sensor - 50kg: Half-wheatstone bridge Load Cell modified from the Fritzing Repo This load sensor, sometimes called a strain gauge, is the same one found in digital bathroom scales (you know, the ones you use in January for your New Year's resolutions, and then forget about a month later). This sensor can measure up to about 110 pounds.
